// Logisim project PKB-08 - Copy.circ as structural Verilog: 5 circuits, main circuit main
module main (
  input  A,
  input  B,
  input  [9:0] Shubuh,
  input  [9:0] Dzuhur,
  input  [9:0] AsharMaghrib,
  input  [9:0] Isya,
  input  Enable,
  input  Switch,
  input  Start,
  input  Rst
);

  wire and_1_out, and_2_out, and_3_out, and_4_out, and_5_out, and_6_out, and_7_out, and_8_out, and_9_out,
       and_10_out, and_11_out, and_12_out, and_13_out, and_14_out, Clk_out, ic7447_1_a, ic7447_1_b,
       ic7447_1_c, ic7447_1_d, ic7447_1_e, ic7447_1_f, ic7447_1_g, ic7447_2_a, ic7447_2_b, ic7447_2_c,
       ic7447_2_d, ic7447_2_e, ic7447_2_f, ic7447_2_g, ic7447_3_a, ic7447_3_b, ic7447_3_c, ic7447_3_d,
       ic7447_3_e, ic7447_3_f, ic7447_3_g, ic7447_4_a, ic7447_4_b, ic7447_4_c, ic7447_4_d, ic7447_4_e,
       ic7447_4_f, ic7447_4_g, ic7493_1_q0, ic7493_1_q1, ic7493_1_q2, ic7493_1_q3, ic7493_2_q0, ic7493_2_q1,
       ic7493_2_q2, ic7493_2_q3, ic7493_3_q0, ic7493_3_q1, ic7493_3_q2, ic7493_3_q3, ic7493_4_q0,
       ic7493_4_q1, ic7493_4_q2, ic7493_4_q3, not_1_out, not_2_out, not_3_out, not_4_out, not_5_out,
       not_6_out, not_7_out, not_8_out, not_9_out, not_10_out, not_11_out, not_12_out, not_13_out,
       not_14_out, not_15_out, not_16_out, not_17_out, not_18_out, or_1_out, or_2_out, or_3_out, or_4_out,
       or_5_out, timer_1_q;
  wire [3:0] binary_to_bcd_converter_1_p2, binary_to_bcd_converter_1_p3, binary_to_bcd_converter_1_p4,
       binary_to_bcd_converter_1_p5;
  wire [9:0] binary_to_bcd_converter_1_p1, mux_1_out_7;

  Clock Clk (.out(Clk_out));
  or or_1 (or_1_out, Rst, and_8_out, and_1_out);
  and and_1 (and_1_out, ic7493_1_q0, ic7493_1_q3);
  IC7493 ic7493_1 (
    .VCC(Start), .CLK(and_2_out), .R(or_1_out), .Q0(ic7493_1_q0), .Q1(ic7493_1_q1), .Q2(ic7493_1_q2),
    .Q3(ic7493_1_q3));
  or or_2 (or_2_out, Rst, and_8_out, and_2_out);
  MUX mux_1 (
    .Input1(A), .Input2(B), .in_3(Shubuh), .in_4(Dzuhur), .in_5(AsharMaghrib), .in_6(Isya),
    .out_7(mux_1_out_7));
  IC7447 ic7447_1 (
    .Switch(Switch), .A3(ic7493_1_q3), .A2(ic7493_1_q2), .A1(ic7493_1_q1), .A0(ic7493_1_q0), .A(ic7447_1_a),
    .B(ic7447_1_b), .C(ic7447_1_c), .D(ic7447_1_d), .E(ic7447_1_e), .F(ic7447_1_f), .G(ic7447_1_g));
  not not_1 (not_1_out, timer_1_q);
  IC7493 ic7493_2 (
    .VCC(Start), .CLK(and_5_out), .R(or_2_out), .Q0(ic7493_2_q0), .Q1(ic7493_2_q1), .Q2(ic7493_2_q2),
    .Q3(ic7493_2_q3));
  and and_2 (and_2_out, ic7493_2_q1, ic7493_2_q3);
  and and_3 (and_3_out, Clk_out, not_1_out);
  and and_4 (and_4_out, ic7493_2_q1, ic7493_2_q0);
  _7_Segment_Display u_7_segment_display_1 (
    .g(ic7447_1_g), .f(ic7447_1_f), .a(ic7447_1_a), .b(ic7447_1_b), .e(ic7447_1_e), .d(ic7447_1_d),
    .c(ic7447_1_c));  // open: dp
  Hex_Digit_Display hex_digit_display_1 (.value(binary_to_bcd_converter_1_p2));  // open: dp
  // Binary_to_BCD_converter #(.binvalue(10)) binary_to_bcd_converter_1: pin names not known; wires that end beside it: binary_to_bcd_converter_1_p1, binary_to_bcd_converter_1_p2, binary_to_bcd_converter_1_p3, binary_to_bcd_converter_1_p4, binary_to_bcd_converter_1_p5
  _7_Segment_Display u_7_segment_display_2 (
    .g(ic7447_2_g), .f(ic7447_2_f), .a(ic7447_2_a), .b(ic7447_2_b), .e(ic7447_2_e), .d(ic7447_2_d),
    .c(ic7447_2_c));  // open: dp
  IC7447 ic7447_2 (
    .Switch(Switch), .A3(ic7493_2_q3), .A2(ic7493_2_q2), .A1(ic7493_2_q1), .A0(ic7493_2_q0), .A(ic7447_2_a),
    .B(ic7447_2_b), .C(ic7447_2_c), .D(ic7447_2_d), .E(ic7447_2_e), .F(ic7447_2_f), .G(ic7447_2_g));
  or or_3 (or_3_out, Rst, and_8_out, and_5_out);
  TIMER timer_1 (
    .reset(Rst), .load(or_5_out), .clk(and_3_out), .max(mux_1_out_7), .q(timer_1_q),
    .outt(binary_to_bcd_converter_1_p1));
  Hex_Digit_Display hex_digit_display_2 (.value(binary_to_bcd_converter_1_p3));  // open: dp
  Hex_Digit_Display hex_digit_display_3 (.value(binary_to_bcd_converter_1_p4));  // open: dp
  _7_Segment_Display u_7_segment_display_3 (
    .g(ic7447_3_g), .f(ic7447_3_f), .a(ic7447_3_a), .b(ic7447_3_b), .e(ic7447_3_e), .d(ic7447_3_d),
    .c(ic7447_3_c));  // open: dp
  Hex_Digit_Display hex_digit_display_4 (.value(binary_to_bcd_converter_1_p5));  // open: dp
  _7_Segment_Display u_7_segment_display_4 (
    .g(ic7447_4_g), .f(ic7447_4_f), .a(ic7447_4_a), .b(ic7447_4_b), .e(ic7447_4_e), .d(ic7447_4_d),
    .c(ic7447_4_c));  // open: dp
  LED led_1 (.in(and_7_out));
  LED led_2 (.in(and_7_out));
  LED led_3 (.in(and_7_out));
  LED led_4 (.in(and_7_out));
  LED led_5 (.in(and_7_out));
  LED led_6 (.in(and_7_out));
  LED led_7 (.in(and_7_out));
  IC7493 ic7493_3 (
    .VCC(Start), .CLK(and_9_out), .R(or_3_out), .Q0(ic7493_3_q0), .Q1(ic7493_3_q1), .Q2(ic7493_3_q2),
    .Q3(ic7493_3_q3));
  and and_5 (and_5_out, ic7493_3_q1, ic7493_3_q2);
  LED led_8 (.in(and_7_out));
  LED led_9 (.in(and_7_out));
  LED led_10 (.in(and_7_out));
  LED led_11 (.in(and_7_out));
  LED led_12 (.in(and_7_out));
  LED led_13 (.in(and_7_out));
  LED led_14 (.in(and_7_out));
  LED led_15 (.in(and_7_out));
  LED led_16 (.in(and_7_out));
  LED led_17 (.in(and_7_out));
  and and_6 (and_6_out, ic7493_3_q2, ic7493_3_q0);
  LED led_18 (.in(and_7_out));
  LED led_19 (.in(and_7_out));
  LED led_20 (.in(and_7_out));
  LED led_21 (.in(and_7_out));
  LED led_22 (.in(and_7_out));
  LED led_23 (.in(and_7_out));
  LED led_24 (.in(and_7_out));
  LED led_25 (.in(and_7_out));
  LED led_26 (.in(and_7_out));
  and and_7 (and_7_out, Enable, timer_1_q);
  LED led_27 (.in(and_7_out));
  LED led_28 (.in(and_7_out));
  LED led_29 (.in(and_7_out));
  LED led_30 (.in(and_7_out));
  LED led_31 (.in(and_7_out));
  LED led_32 (.in(and_7_out));
  LED led_33 (.in(and_7_out));
  LED led_34 (.in(and_7_out));
  LED led_35 (.in(and_7_out));
  LED led_36 (.in(and_7_out));
  LED led_37 (.in(and_7_out));
  LED led_38 (.in(and_7_out));
  LED led_39 (.in(and_7_out));
  LED led_40 (.in(and_7_out));
  LED led_41 (.in(and_7_out));
  LED led_42 (.in(and_7_out));
  IC7447 ic7447_3 (
    .Switch(Switch), .A3(ic7493_3_q3), .A2(ic7493_3_q2), .A1(ic7493_3_q1), .A0(ic7493_3_q0), .A(ic7447_3_a),
    .B(ic7447_3_b), .C(ic7447_3_c), .D(ic7447_3_d), .E(ic7447_3_e), .F(ic7447_3_f), .G(ic7447_3_g));
  or or_4 (or_4_out, Rst, and_8_out, and_9_out);
  and and_8 (and_8_out, and_6_out, ic7493_4_q3, and_4_out, ic7493_1_q1);
  LED led_43 (.in(and_7_out));
  LED led_44 (.in(and_7_out));
  LED led_45 (.in(and_7_out));
  LED led_46 (.in(and_7_out));
  LED led_47 (.in(and_7_out));
  LED led_48 (.in(and_7_out));
  LED led_49 (.in(and_7_out));
  LED led_50 (.in(and_7_out));
  LED led_51 (.in(and_7_out));
  LED led_52 (.in(and_7_out));
  LED led_53 (.in(and_7_out));
  LED led_54 (.in(and_7_out));
  LED led_55 (.in(and_7_out));
  LED led_56 (.in(and_7_out));
  LED led_57 (.in(and_7_out));
  LED led_58 (.in(and_7_out));
  LED led_59 (.in(and_7_out));
  LED led_60 (.in(and_7_out));
  and and_9 (and_9_out, ic7493_4_q1, ic7493_4_q3);
  // Buzzer buzzer_1: pin names not known; wires that end beside it: and_7_out, and_7_out, and_7_out, and_7_out, and_7_out, and_7_out, and_7_out, and_7_out, and_7_out, and_7_out, and_7_out, and_7_out, and_7_out, {7{1'b1}}
  IC7493 ic7493_4 (
    .VCC(Start), .CLK(Clk_out), .R(or_4_out), .Q0(ic7493_4_q0), .Q1(ic7493_4_q1), .Q2(ic7493_4_q2),
    .Q3(ic7493_4_q3));
  IC7447 ic7447_4 (
    .Switch(Switch), .A3(ic7493_4_q3), .A2(ic7493_4_q2), .A1(ic7493_4_q1), .A0(ic7493_4_q0), .A(ic7447_4_a),
    .B(ic7447_4_b), .C(ic7447_4_c), .D(ic7447_4_d), .E(ic7447_4_e), .F(ic7447_4_f), .G(ic7447_4_g));
  and and_10 (and_10_out, ic7447_4_b, Enable, not_2_out, not_3_out, not_4_out, not_5_out);
  not not_2 (not_2_out, ic7447_4_g);
  not not_3 (not_3_out, ic7447_3_g);
  not not_4 (not_4_out, ic7447_2_g);
  not not_5 (not_5_out, ic7447_1_g);
  and and_11 (and_11_out, Enable, ic7447_3_g, ic7447_3_d, ic7447_3_c, ic7447_2_f, not_2_out, ic7447_2_g, not_6_out, not_7_out);
  not not_6 (not_6_out, ic7447_3_f);
  not not_7 (not_7_out, ic7447_3_e);
  not not_8 (not_8_out, ic7447_1_f);
  or or_5 (or_5_out, and_10_out, and_11_out, and_12_out, and_13_out, and_14_out);
  and and_12 (and_12_out, Enable, not_8_out, ic7447_3_c, not_2_out, ic7447_3_d, ic7447_2_g, not_9_out, not_10_out, not_11_out, ic7447_2_e, ic7447_1_c, ic7447_1_b);
  not not_9 (not_9_out, ic7447_3_e);
  not not_10 (not_10_out, ic7447_3_f);
  not not_11 (not_11_out, ic7447_2_f);
  and and_13 (and_13_out, Enable, not_2_out, ic7447_3_d, ic7447_2_g, not_12_out, not_13_out, ic7447_1_b, ic7447_1_c, not_14_out, ic7447_2_d, ic7447_2_c, not_15_out);
  not not_12 (not_12_out, ic7447_3_f);
  not not_13 (not_13_out, ic7447_3_e);
  not not_14 (not_14_out, ic7447_1_f);
  not not_15 (not_15_out, ic7447_2_e);
  and and_14 (and_14_out, Enable, not_2_out, ic7447_3_d, ic7447_2_g, not_16_out, not_17_out, ic7447_1_b, ic7447_1_c, not_18_out, ic7447_2_f, ic7447_2_e, ic7447_2_d);
  not not_16 (not_16_out, ic7447_3_f);
  not not_17 (not_17_out, ic7447_3_e);
  not not_18 (not_18_out, ic7447_1_f);

  // Notes on the sheet:
  //   6. Ubah MUX menjadi waktu Dzuhur
  //   CARA KERJA
  //   1. Ubah konfigurasi biner seperti yang dibawah
  //   2. Tekan Switch,Enable, dan mulai simulasi clock nya
  //   4. Ketika T-30 nyalakan enable dan lampu akan menyala 
  //   5. Ketika lampu mati matikan enable lagi 
  //   7. Ulangi langkah ke 3 sampai 5 dengan urutan MUX : 
  //   a) Waktu Shubuh A = 0, B = 0
  //   b) Waktu Dzuhur A = 1, B = 0
  //   c) Waktu Ashar A = 0, B = 1
  //   d) Waktu Maghrib A = 0, B = 1
  //   e) Waktu Isya A = 1, B = 1
  //   3. Tekan Start lalu matikan enable serta ubah MUX menjadi Waktu Shubuh
  //   Konfigurasi Shubuh = 0011110000
  //   Konfigurasi Dzuhur = 0110111100
  //   Konfigurasi Ashar Maghrib = 0010100000
  //   Konfigurasi Isya = 0000110000
endmodule

module IC7447 (
  input  Switch,
  input  A3,
  input  A2,
  input  A1,
  input  A0,
  output A,
  output B,
  output C,
  output D,
  output E,
  output F,
  output G
);

  wire and_1_out, and_2_out, and_3_out, and_4_out, and_5_out, and_6_out, and_7_out, and_8_out, and_9_out,
       and_10_out, and_11_out, and_12_out, and_13_out, and_14_out, not_1_out, not_2_out, not_3_out,
       not_4_out, or_1_out, or_2_out, or_3_out, or_4_out, or_5_out, or_6_out, or_7_out;

  not not_1 (not_1_out, A3);
  not not_2 (not_2_out, A2);
  not not_3 (not_3_out, A1);
  not not_4 (not_4_out, A0);
  and and_1 (and_1_out, A3, not_2_out, not_3_out);
  and and_2 (and_2_out, not_1_out, not_2_out, A1);
  and and_3 (and_3_out, not_1_out, A2, not_3_out);
  and and_4 (and_4_out, not_1_out, not_4_out, A1);
  and and_5 (and_5_out, not_3_out, not_1_out, not_4_out);
  and and_6 (and_6_out, not_2_out, not_3_out, not_4_out);
  and and_7 (and_7_out, not_1_out, A1);
  and and_8 (and_8_out, A2, not_1_out, A0);
  and and_9 (and_9_out, not_1_out, not_2_out);
  and and_10 (and_10_out, not_1_out, A1, A0);
  and and_11 (and_11_out, not_1_out, A2);
  and and_12 (and_12_out, not_1_out, A0);
  and and_13 (and_13_out, and_3_out, A0);
  and and_14 (and_14_out, not_1_out, not_4_out, A2);
  or or_1 (or_1_out, and_7_out, and_1_out, and_6_out, and_8_out);
  or or_2 (or_2_out, and_1_out, and_5_out, and_9_out, and_10_out);
  or or_3 (or_3_out, and_1_out, and_6_out, and_11_out, and_12_out);
  or or_4 (or_4_out, and_6_out, and_2_out, and_1_out, and_4_out, and_13_out);
  or or_5 (or_5_out, and_4_out, and_6_out);
  or or_6 (or_6_out, and_14_out, and_3_out, and_5_out, and_1_out);
  or or_7 (or_7_out, and_1_out, and_3_out, and_4_out, and_2_out);
  and and_15 (A, or_1_out, Switch);
  and and_16 (B, or_2_out, Switch);
  and and_17 (C, or_3_out, Switch);
  and and_18 (D, or_4_out, Switch);
  and and_19 (E, Switch, or_5_out);
  and and_20 (F, Switch, or_6_out);
  and and_21 (G, or_7_out, Switch);
endmodule

module IC7493 (
  input  VCC,
  input  CLK,
  input  R,
  output Q0,
  output Q1,
  output Q2,
  output Q3
);

  wire not_1_out, not_2_out, not_3_out, not_4_out;

  J_K_Flip_Flop j_k_ff_1 (.J(VCC), .K(VCC), .clk(not_1_out), .Q(Q0), .reset(R));  // open: Qn, preset
  not not_1 (not_1_out, CLK);
  J_K_Flip_Flop j_k_ff_2 (.J(VCC), .K(VCC), .clk(not_2_out), .Q(Q1), .reset(R));  // open: Qn, preset
  not not_2 (not_2_out, Q0);
  J_K_Flip_Flop j_k_ff_3 (.J(VCC), .K(VCC), .clk(not_3_out), .Q(Q2), .reset(R));  // open: Qn, preset
  not not_3 (not_3_out, Q1);
  J_K_Flip_Flop j_k_ff_4 (.J(VCC), .K(VCC), .clk(not_4_out), .Q(Q3), .reset(R));  // open: Qn, preset
  not not_4 (not_4_out, Q2);
endmodule

module MUX (
  input  Input1,
  input  Input2,
  input  [9:0] in_3,
  input  [9:0] in_4,
  input  [9:0] in_5,
  input  [9:0] in_6,
  output [9:0] out_7
);

  wire [9:0] and_1_out, and_2_out, and_3_out, and_4_out, bit_extender_1_out, bit_extender_2_out, not_1_out,
       not_2_out;

  assign bit_extender_1_out = {{9{Input1}}, Input1};  // Bit_Extender bit_extender_1
  assign bit_extender_2_out = {{9{Input2}}, Input2};  // Bit_Extender bit_extender_2
  assign not_1_out = ~bit_extender_1_out;  // NOT_Gate not_1, 10 bits wide
  assign not_2_out = ~bit_extender_2_out;  // NOT_Gate not_2, 10 bits wide
  assign and_1_out = in_3 & not_2_out & not_1_out;  // AND_Gate and_1, 10 bits wide
  assign and_2_out = in_4 & not_2_out & bit_extender_1_out;  // AND_Gate and_2, 10 bits wide
  assign and_3_out = in_5 & bit_extender_2_out & not_1_out;  // AND_Gate and_3, 10 bits wide
  assign and_4_out = in_6 & bit_extender_1_out & bit_extender_2_out;  // AND_Gate and_4, 10 bits wide
  assign out_7 = and_1_out | and_2_out | and_3_out | and_4_out;  // OR_Gate or_1, 10 bits wide
endmodule

module TIMER (
  input  reset,
  input  load,
  input  clk,
  input  [9:0] max,
  output q,
  output [9:0] outt
);

  Counter #(.max('h3ff), .width(10)) counter_1 (
    .clr(reset), .load(load), .up(load), .clk(clk), .D(max), .carry(q), .Q(outt));  // open: count
endmodule
